// Logisim project Lab_4.circ as structural Verilog
module \Процессор  (
  input  HALT,
  input  \ЗагрАдрИнстр ,
  input  \РежимСчет ,
  input  \Сброс ,
  input  \ЗапRAM ,
  input  \ЗагрINSTR ,
  input  \ИстTEMP ,
  input  \ЗагрTEMP ,
  input  \ВыборДругРег ,
  input  \СохрРегA_B 
);

  wire and_1_out, demultiplexer_2_out0, demultiplexer_2_out1, NF, not_1_out, not_2_out, not_3_out, not_4_out,
       OF, xor_1_out, ZF, \Такты_out ;
  wire [15:0] ADDRESS, counter_1_q, INSTR_q, multiplexer_1_out, multiplexer_2_out;
  wire [31:0] A_q, ACC, \alu_32_бит_1_выход , B_q, demultiplexer_1_out0, demultiplexer_1_out1,
       multiplexer_3_out, multiplexer_4_out, multiplexer_5_out, ram_1_data, TEMP_q;

  Clock \u_Такты  (.out(\Такты_out ));
  Multiplexer #(.width(16), .enable("false")) multiplexer_1 (
    .in0(counter_1_q), .in1(ADDRESS), .out(multiplexer_1_out), .sel(\ЗагрАдрИнстр ));
  and and_1 (and_1_out, \Такты_out , HALT);
  Counter #(.width(16), .max('hffff), .trigger("falling")) counter_1 (
    .load(\РежимСчет ), .D(multiplexer_1_out), .count(not_1_out), .Q(counter_1_q), .clk(and_1_out),
    .clr(\Сброс ));  // open: carry
  not not_1 (not_1_out, \РежимСчет );
  not not_2 (not_2_out, and_1_out);
  Multiplexer #(.width(16), .enable("false")) multiplexer_2 (
    .in0(ADDRESS), .in1(counter_1_q), .out(multiplexer_2_out), .sel(not_2_out));
  not not_3 (not_3_out, and_1_out);
  RAM #(.addrWidth(16), .dataWidth(32), .bus("separate")) ram_1 (
    .addr(multiplexer_2_out), .din(ACC), .data(ram_1_data), .str(\ЗапRAM ), .clk(not_3_out));  // open: sel, ld, clr
  Register #(.width(16)) INSTR (.D(ram_1_data[31:16]), .en(\ЗагрINSTR ), .Q(INSTR_q), .clk(and_1_out), .clr(\Сброс ));
  Register #(.width(16)) u_ADDRESS (
    .D(ram_1_data[15:0]), .en(\ЗагрINSTR ), .Q(ADDRESS), .clk(and_1_out), .clr(\Сброс ));
  Multiplexer #(.width(32), .enable("false")) multiplexer_3 (
    .in0(ram_1_data), .in1(ACC), .out(multiplexer_3_out), .sel(\ИстTEMP ));
  Register #(.width(32), .trigger("falling")) TEMP (
    .D(multiplexer_3_out), .en(\ЗагрTEMP ), .Q(TEMP_q), .clk(and_1_out), .clr(\Сброс ));
  Multiplexer #(.width(32), .enable("false")) multiplexer_4 (
    .in0(TEMP_q), .in1(ACC), .out(multiplexer_4_out), .sel(INSTR_q[4]));
  Multiplexer #(.width(32), .enable("false")) multiplexer_5 (
    .in0(TEMP_q), .in1(ACC), .out(multiplexer_5_out), .sel(not_4_out));
  not not_4 (not_4_out, INSTR_q[4]);
  xor xor_1 (xor_1_out, INSTR_q[5], \ВыборДругРег );
  Demultiplexer #(.width(32), .enable("false")) demultiplexer_1 (
    .out0(demultiplexer_1_out0), .out1(demultiplexer_1_out1), .in(\alu_32_бит_1_выход ), .sel(xor_1_out));
  \ALU_32_бит  \alu_32_бит_1  (
    .A(multiplexer_4_out), .B(multiplexer_5_out), .\Выбор_команды (INSTR_q[3:0]), .Zero_Flag(ZF),
    .Negative_Flag(NF), .\Выход (\alu_32_бит_1_выход ), .Overflow_Flag(OF));
  Demultiplexer #(.enable("false")) demultiplexer_2 (
    .out0(demultiplexer_2_out0), .out1(demultiplexer_2_out1), .in(\СохрРегA_B ), .sel(xor_1_out));
  Register #(.width(32)) A (
    .D(demultiplexer_1_out0), .en(demultiplexer_2_out0), .Q(A_q), .clk(and_1_out), .clr(\Сброс ));
  Register #(.width(32)) B (
    .D(demultiplexer_1_out1), .en(demultiplexer_2_out1), .Q(B_q), .clk(and_1_out), .clr(\Сброс ));
  Multiplexer #(.width(32), .enable("false")) multiplexer_6 (.in0(A_q), .in1(B_q), .out(ACC), .sel(xor_1_out));

  // Other names for the same wires on the sheet: RESET = \Сброс 
endmodule

module \ALU_32_бит  (
  input  [31:0] A,
  input  [31:0] B,
  input  [3:0] \Выбор_команды ,
  output Zero_Flag,
  output Negative_Flag,
  output [31:0] \Выход ,
  output Overflow_Flag
);

  wire comparator_1_lt, comparator_2_gt, comparator_3_eq, not_2_out, not_3_out;
  wire [31:0] adder_1_out, and_1_out, divider_1_out, multiplexer_1_out, multiplexer_2_out, multiplexer_3_out,
       multiplier_1_out, not_1_out, or_1_out, shifter_1_out, subtractor_1_out, xor_1_out;

  // Probe on A
  // Probe on B
  // Probe on \Выбор_команды 
  assign not_1_out = ~A;  // NOT_Gate not_1, 32 bits wide
  assign and_1_out = A & B;  // AND_Gate and_1, 32 bits wide
  assign or_1_out = A | B;  // OR_Gate or_1, 32 bits wide
  assign xor_1_out = A ^ B;  // XOR_Gate xor_1, 32 bits wide
  Multiplier #(.width(32)) multiplier_1 (.a(A), .b(B), .out(multiplier_1_out));  // open: cin, cout
  Divider #(.width(32)) divider_1 (.a(A), .b(B), .out(divider_1_out));  // open: upper, rem
  Subtractor #(.width(32)) subtractor_1 (.a(A), .b(B), .out(subtractor_1_out));  // open: bin, bout
  Adder #(.width(32)) adder_1 (.a(A), .b(B), .out(adder_1_out), .cout(Overflow_Flag));  // open: cin
  Comparator #(.width(32)) comparator_1 (.a(A), .b(B), .lt(comparator_1_lt));  // open: gt, eq
  Comparator #(.width(32)) comparator_2 (.a(A), .b(B), .gt(comparator_2_gt));  // open: eq, lt
  Comparator #(.width(32)) comparator_3 (.a(A), .b(B), .eq(comparator_3_eq));  // open: gt, lt
  Shifter #(.width(32)) shifter_1 (.in(A), .\dist (5'b00001), .out(shifter_1_out));
  Multiplexer #(.width(32), .enable("false")) multiplexer_1 (
    .in0(A), .in1(B), .out(multiplexer_1_out), .sel(not_2_out));
  not not_2 (not_2_out, comparator_1_lt);
  Multiplexer #(.width(32), .enable("false")) multiplexer_2 (
    .in0(A), .in1(B), .out(multiplexer_2_out), .sel(not_3_out));
  not not_3 (not_3_out, comparator_2_gt);
  Multiplexer #(.width(32), .enable("false")) multiplexer_3 (
    .in0({32{1'b0}}), .in1({32{1'b1}}), .out(multiplexer_3_out), .sel(comparator_3_eq));
  Multiplexer #(.select(4), .width(32), .enable("false")) multiplexer_4 (
    .in0(A), .in1(not_1_out), .in2(and_1_out), .in3(or_1_out), .in4(xor_1_out), .in5(multiplier_1_out),
    .in6(divider_1_out), .in7(subtractor_1_out), .in8(adder_1_out), .in9(multiplexer_1_out),
    .in10(multiplexer_2_out), .in11(multiplexer_3_out), .in12(shifter_1_out), .in13({32{1'b0}}),
    .in14({32{1'b0}}), .in15({32{1'b0}}), .out({Negative_Flag, \Выход [30:0]}), .sel(\Выбор_команды ));
  // Probe on {Negative_Flag, \Выход [30:0]}
  nor nor_1 (Zero_Flag, \Выход [15], \Выход [0], \Выход [1], \Выход [2], \Выход [3], \Выход [4], \Выход [5], \Выход [6], \Выход [7], \Выход [8], \Выход [9], \Выход [10], \Выход [11], \Выход [12], \Выход [13], \Выход [14], \Выход [16], \Выход [17], \Выход [18], \Выход [19], \Выход [20], \Выход [21], \Выход [22], \Выход [23], \Выход [24], \Выход [25], \Выход [26], \Выход [27], \Выход [28], \Выход [29], \Выход [30], Negative_Flag);

  assign \Выход [31] = Negative_Flag;

  // Notes on the sheet:
  //   Список команд:
  //   0 = A
  //   1 = NOT(A)
  //   2 = A AND B
  //   3 = A OR B
  //   4 = A XOR B
  //   5 = A x B
  //   6 = A / B
  //   7 = A - B
  //   8 = A + B
  //   9 = MIN(A, B)
  //   10 = MAX(A, B)
  //   11 = (A = B)?
  //   12 = A << 1
endmodule

module S_Fetch (
  input  in_1,
  input  in_2,
  input  in_3,
  input  in_4,
  input  in_5,
  input  in_6,
  input  in_7,
  input  in_8,
  input  in_9,
  input  in_10,
  output out_11,
  output out_12,
  output out_13,
  output out_14,
  output out_15
);
endmodule
