// Logisim project Timer.circ as structural Verilog: 13 circuits, main circuit Timer
module Timer (
  input  in_1,
  input  in_2
);

  wire _1_out, _2_out, _3_out, _4_out, _5_out, _6_out, _7_out, _8_out, _9_out, button_2_out, button_out,
       clock_1_out, multiplexer_1_out;
  wire [3:0] multiplexer_2_out, multiplexer_2_out_2, multiplexer_3_out, multiplexer_3_out_2,
       multiplexer_4_out, multiplexer_4_out_2, multiplexer_5_out, multiplexer_5_out_2, multiplexer_6_out,
       multiplexer_6_out_2, multiplexer_7_out, multiplexer_7_out_2, \часовой_механизм_1_out_6 ,
       \часовой_механизм_1_out_7 , \часовой_механизм_1_out_8 , \часовой_механизм_1_out_9 ,
       \часовой_механизм_1_out_10 , \часовой_механизм_1_out_11 ;
  wire [7:0] n10_7_1_out_2, n10_7_2_out_2, n10_7_3_out_2, n10_7_4_out_2, n10_7_5_out_2, n10_7_6_out_2;

  Clock clock_1 (.out(clock_1_out));
  Multiplexer #(.enable("false")) multiplexer_1 (.in0(clock_1_out), .in1(in_1), .out(multiplexer_1_out), .sel(in_2));
  Button _1 (.out(_1_out));
  Button _4 (.out(_4_out));
  Button _7 (.out(_7_out));
  Button _8 (.out(_8_out));
  Button button (.out(button_out));
  \Часовой_механизм  \u_часовой_механизм_1  (
    .in_1(multiplexer_1_out), .out_6(\часовой_механизм_1_out_6 ), .out_7(\часовой_механизм_1_out_7 ),
    .out_8(\часовой_механизм_1_out_8 ), .out_9(\часовой_механизм_1_out_9 ),
    .out_10(\часовой_механизм_1_out_10 ), .out_11(\часовой_механизм_1_out_11 ));  // open: in_2, in_5, in_4, in_3
  Button _2 (.out(_2_out));
  Button _3 (.out(_3_out));
  Button _6 (.out(_6_out));
  Button _5 (.out(_5_out));
  Button _9 (.out(_9_out));
  Button button_2 (.out(button_2_out));
  Button _0 ();  // open: out
  _10____7 u_10_7_1 (.out_2(n10_7_1_out_2), .in_1(\часовой_механизм_1_out_6 ));
  Multiplexer #(.width(8), .disabled(0), .enable("false")) multiplexer_2 (
    .in0(n10_7_1_out_2), .in1({8{1'b0}}), .out({multiplexer_2_out_2, multiplexer_2_out}));  // open: sel
  _10____7 u_10_7_2 (.out_2(n10_7_2_out_2), .in_1(\часовой_механизм_1_out_7 ));
  Multiplexer #(.width(8), .disabled(0), .enable("false")) multiplexer_3 (
    .in0(n10_7_2_out_2), .in1({8{1'b0}}), .out({multiplexer_3_out_2, multiplexer_3_out}));  // open: sel
  _10____7 u_10_7_3 (.out_2(n10_7_3_out_2), .in_1(\часовой_механизм_1_out_8 ));
  _10____7 u_10_7_4 (.out_2(n10_7_4_out_2), .in_1(\часовой_механизм_1_out_9 ));
  Multiplexer #(.width(8), .disabled(0), .enable("false")) multiplexer_4 (
    .in0(n10_7_3_out_2), .in1({8{1'b0}}), .out({multiplexer_4_out_2, multiplexer_4_out}));  // open: sel
  _10____7 u_10_7_5 (.out_2(n10_7_5_out_2), .in_1(\часовой_механизм_1_out_10 ));
  Multiplexer #(.width(8), .disabled(0), .enable("false")) multiplexer_5 (
    .in0(n10_7_4_out_2), .in1({8{1'b0}}), .out({multiplexer_5_out_2, multiplexer_5_out}));  // open: sel
  Multiplexer #(.width(8), .disabled(0), .enable("false")) multiplexer_6 (
    .in0(n10_7_5_out_2), .in1({8{1'b0}}), .out({multiplexer_6_out, multiplexer_6_out_2}));  // open: sel
  _10____7 u_10_7_6 (.out_2(n10_7_6_out_2), .in_1(\часовой_механизм_1_out_11 ));
  Multiplexer #(.width(8), .disabled(0), .enable("false")) multiplexer_7 (
    .in0(n10_7_6_out_2), .in1({8{1'b0}}), .out({multiplexer_7_out, multiplexer_7_out_2}));  // open: sel
endmodule

module \Улучшенный_счетчик_4_бит  (
  input  \Счет_вверх_вниз ,
  input  Clock,
  input  Enable,
  input  \Сброс ,
  input  \Запись ,
  input  [3:0] in_6,
  output [3:0] out_7
);

  wire and_1_out, and_2_out, and_3_out, and_4_out, and_5_out, and_6_out, demultiplexer_1_out0,
       demultiplexer_1_out1, demultiplexer_2_out0, demultiplexer_2_out1, demultiplexer_3_out0,
       demultiplexer_3_out1, demultiplexer_4_out0, demultiplexer_4_out1, or_1_out, or_2_out, or_3_out,
       or_4_out, or_5_out, or_6_out, or_7_out, t_ff_1_qn, t_ff_2_qn, t_ff_3_qn;

  Demultiplexer demultiplexer_1 (
    .out0(demultiplexer_1_out0), .out1(demultiplexer_1_out1), .in(\Запись ), .sel(in_6[0]));  // open: en
  and and_1 (and_1_out, \Счет_вверх_вниз , out_7[0]);
  T_Flip_Flop t_ff_1 (
    .clk(Clock), .T(1'b1), .Q(out_7[0]), .Qn(t_ff_1_qn), .preset(demultiplexer_1_out1), .reset(or_1_out),
    .en(Enable));
  and and_2 (and_2_out, t_ff_1_qn, ~\Счет_вверх_вниз );  // AND_Gate
  or or_1 (or_1_out, demultiplexer_1_out0, \Сброс );
  or or_2 (or_2_out, and_1_out, and_2_out);
  Demultiplexer demultiplexer_2 (
    .out0(demultiplexer_2_out0), .out1(demultiplexer_2_out1), .in(\Запись ), .sel(in_6[1]));  // open: en
  and and_3 (and_3_out, and_1_out, out_7[1]);
  T_Flip_Flop t_ff_2 (
    .clk(Clock), .T(or_2_out), .Q(out_7[1]), .Qn(t_ff_2_qn), .preset(demultiplexer_2_out1), .reset(or_3_out),
    .en(Enable));
  and and_4 (and_4_out, t_ff_2_qn, and_2_out);
  or or_3 (or_3_out, demultiplexer_2_out0, \Сброс );
  or or_4 (or_4_out, and_3_out, and_4_out);
  Demultiplexer demultiplexer_3 (
    .out0(demultiplexer_3_out0), .out1(demultiplexer_3_out1), .in(\Запись ), .sel(in_6[2]));  // open: en
  T_Flip_Flop t_ff_3 (
    .clk(Clock), .T(or_4_out), .Q(out_7[2]), .Qn(t_ff_3_qn), .preset(demultiplexer_3_out1), .reset(or_5_out),
    .en(Enable));
  or or_5 (or_5_out, demultiplexer_3_out0, \Сброс );
  and and_5 (and_5_out, and_3_out, out_7[2]);
  or or_6 (or_6_out, and_5_out, and_6_out);
  and and_6 (and_6_out, t_ff_3_qn, and_4_out);
  T_Flip_Flop t_ff_4 (
    .clk(Clock), .T(or_6_out), .Q(out_7[3]), .preset(demultiplexer_4_out1), .reset(or_7_out), .en(Enable));  // open: Qn
  or or_7 (or_7_out, demultiplexer_4_out0, \Сброс );
  Demultiplexer demultiplexer_4 (
    .out0(demultiplexer_4_out0), .out1(demultiplexer_4_out1), .in(\Запись ), .sel(in_6[3]));  // open: en
endmodule

module \Сравнение_границы  (
  input  [3:0] in_1,
  input  [3:0] in_2,
  output out_3
);

  wire not_1_out, not_2_out, not_3_out, not_4_out, xor_1_out, xor_2_out, xor_3_out, xor_4_out;

  xor xor_1 (xor_1_out, in_1[0], in_2[0]);
  not not_1 (not_1_out, xor_1_out);
  xor xor_2 (xor_2_out, in_1[1], in_2[1]);
  not not_2 (not_2_out, xor_2_out);
  xor xor_3 (xor_3_out, in_1[2], in_2[2]);
  not not_3 (not_3_out, xor_3_out);
  xor xor_4 (xor_4_out, in_1[3], in_2[3]);
  not not_4 (not_4_out, xor_4_out);
  and and_1 (out_3, not_1_out, not_2_out, not_3_out, not_4_out);
endmodule

module \Ограничитель_0_9  (
  input  in_1,
  input  in_2,
  input  in_3,
  input  [3:0] in_4,
  output [3:0] out_5
);

  wire and_1_out, \сравнение_границы_1_out_3 ;

  and and_1 (and_1_out, in_1, \сравнение_границы_1_out_3 );
  \Улучшенный_счетчик_4_бит  \u_улучшенный_счетчик_4_бит_1  (
    .\Счет_вверх_вниз (1'b0), .Clock(in_1), .Enable(in_2), .\Сброс (in_3), .\Запись (and_1_out),
    .out_7(in_4), .in_6(4'b1001));
  \Сравнение_границы  \u_сравнение_границы_1  (.in_1(in_4), .in_2(4'b1111), .out_3(\сравнение_границы_1_out_3 ));

  assign out_5 = in_4;
endmodule

module \Ограничитель_0_5  (
  input  in_1,
  input  in_2,
  input  in_3,
  input  [3:0] in_4,
  output [3:0] out_5
);

  wire and_1_out, \сравнение_границы_1_out_3 ;

  and and_1 (and_1_out, in_1, \сравнение_границы_1_out_3 );
  \Улучшенный_счетчик_4_бит  \u_улучшенный_счетчик_4_бит_1  (
    .\Счет_вверх_вниз (1'b0), .Clock(in_1), .Enable(in_2), .\Сброс (in_3), .\Запись (and_1_out),
    .out_7(in_4), .in_6(4'b0101));
  \Сравнение_границы  \u_сравнение_границы_1  (.in_1(in_4), .in_2(4'b1111), .out_3(\сравнение_границы_1_out_3 ));

  assign out_5 = in_4;
endmodule

module \Часовой_механизм  (
  input  in_1,
  input  in_2,
  input  in_3,
  input  [2:0] in_4,
  input  [3:0] in_5,
  output [3:0] out_6,
  output [3:0] out_7,
  output [3:0] out_8,
  output [3:0] out_9,
  output [3:0] out_10,
  output [3:0] out_11
);

  wire \сравнение_границы_1_out_3 , \сравнение_границы_2_out_3 , \сравнение_границы_3_out_3 ,
       \сравнение_границы_4_out_3 , \сравнение_границы_5_out_3 ;
  wire [3:0] demultiplexer_1_out0, demultiplexer_1_out1, demultiplexer_1_out2, demultiplexer_1_out3,
       demultiplexer_1_out4, demultiplexer_1_out5;

  // Probe on out_6
  \Ограничитель_0_9  \u_ограничитель_0_9_1  (
    .in_1(\сравнение_границы_1_out_3 ), .in_2(in_1), .in_3(in_2), .out_5(out_6), .in_4(demultiplexer_1_out5));
  \Сравнение_границы  \u_сравнение_границы_1  (.in_1(out_7), .in_2(4'b1001), .out_3(\сравнение_границы_1_out_3 ));
  // Probe on out_7
  \Ограничитель_0_9  \u_ограничитель_0_9_2  (
    .in_1(\сравнение_границы_2_out_3 ), .in_2(in_1), .in_3(in_2), .out_5(out_7), .in_4(demultiplexer_1_out4));
  \Сравнение_границы  \u_сравнение_границы_2  (.in_1(out_8), .in_2(4'b0101), .out_3(\сравнение_границы_2_out_3 ));
  // Probe on out_8
  \Ограничитель_0_5  \u_ограничитель_0_5_1  (
    .in_1(\сравнение_границы_3_out_3 ), .in_2(in_1), .in_3(in_2), .out_5(out_8), .in_4(demultiplexer_1_out3));
  Demultiplexer #(.select(3), .width(4), .enable("false")) demultiplexer_1 (
    .out0(demultiplexer_1_out0), .out1(demultiplexer_1_out1), .out2(demultiplexer_1_out2),
    .out3(demultiplexer_1_out3), .out4(demultiplexer_1_out4), .out5(demultiplexer_1_out5), .in(in_5),
    .sel(in_4));  // open: out6, out7
  \Сравнение_границы  \u_сравнение_границы_3  (.in_1(out_9), .in_2(4'b1001), .out_3(\сравнение_границы_3_out_3 ));
  // Probe on out_9
  \Ограничитель_0_9  \u_ограничитель_0_9_3  (
    .in_1(\сравнение_границы_4_out_3 ), .in_2(in_1), .in_3(in_2), .out_5(out_9), .in_4(demultiplexer_1_out2));
  \Сравнение_границы  \u_сравнение_границы_4  (.in_1(out_10), .in_2(4'b0101), .out_3(\сравнение_границы_4_out_3 ));
  // Probe on out_10
  \Ограничитель_0_5  \u_ограничитель_0_5_2  (
    .in_1(\сравнение_границы_5_out_3 ), .in_2(in_1), .in_3(in_2), .out_5(out_10), .in_4(demultiplexer_1_out1));
  \Сравнение_границы  \u_сравнение_границы_5  (.in_1(out_11), .in_2(4'b1001), .out_3(\сравнение_границы_5_out_3 ));
  // Probe on out_11
  \Ограничитель_0_9  \u_ограничитель_0_9_4  (
    .in_1(in_3), .in_2(in_1), .in_3(in_2), .out_5(out_11), .in_4(demultiplexer_1_out0));
endmodule

module \Перевод_в_10_ричную  (
  input  _0,
  input  _1,
  input  _2,
  input  _3,
  input  _4,
  input  _5,
  input  _6,
  input  _7,
  input  _8,
  input  _9,
  output [3:0] out_11
);

  \Бит_0  \u_бит_0_1  (.in_1({_9, _8, _7, _6, _5, _4, _3, _2, _1, _0}), .out_2(out_11[0]));
  \Бит_1  \u_бит_1_1  (.in_1({_9, _8, _7, _6, _5, _4, _3, _2, _1, _0}), .out_2(out_11[1]));
  \Бит_2  \u_бит_2_1  (.in_1({_9, _8, _7, _6, _5, _4, _3, _2, _1, _0}), .out_2(out_11[2]));
  \Бит_3  \u_бит_3_1  (.in_1({_9, _8, _7, _6, _5, _4, _3, _2, _1, _0}), .out_2(out_11[3]));
  // Probe on out_11
endmodule

module \Бит_3  (
  input  [9:0] in_1,
  output out_2
);

  wire and_1_out, and_2_out;

  and and_1 (and_1_out, ~in_1[0], ~in_1[1], ~in_1[2], ~in_1[3], ~in_1[4], ~in_1[5], ~in_1[6], ~in_1[7], ~in_1[8], in_1[9]);  // AND_Gate
  and and_2 (and_2_out, ~in_1[0], ~in_1[1], ~in_1[2], ~in_1[3], ~in_1[4], ~in_1[5], ~in_1[6], ~in_1[7], in_1[8], ~in_1[9]);  // AND_Gate
  or or_1 (out_2, and_1_out, and_2_out);
endmodule

module \Бит_2  (
  input  [9:0] in_1,
  output out_2
);

  wire and_1_out, and_2_out, and_3_out, and_4_out;

  and and_1 (and_1_out, ~in_1[0], ~in_1[1], ~in_1[2], ~in_1[3], ~in_1[4], ~in_1[5], ~in_1[6], in_1[7], ~in_1[8], ~in_1[9]);  // AND_Gate
  and and_2 (and_2_out, ~in_1[0], ~in_1[1], ~in_1[2], ~in_1[3], ~in_1[4], ~in_1[5], in_1[6], ~in_1[7], ~in_1[8], ~in_1[9]);  // AND_Gate
  and and_3 (and_3_out, ~in_1[0], ~in_1[1], ~in_1[2], ~in_1[3], ~in_1[4], in_1[5], ~in_1[6], ~in_1[7], ~in_1[8], ~in_1[9]);  // AND_Gate
  and and_4 (and_4_out, ~in_1[0], ~in_1[1], ~in_1[2], ~in_1[3], in_1[4], ~in_1[5], ~in_1[6], ~in_1[7], ~in_1[8], ~in_1[9]);  // AND_Gate
  or or_1 (out_2, and_1_out, and_2_out, and_3_out, and_4_out);
endmodule

module \Бит_1  (
  input  [9:0] in_1,
  output out_2
);

  wire and_1_out, and_2_out, and_3_out, and_4_out;

  and and_1 (and_1_out, ~in_1[0], ~in_1[1], ~in_1[2], ~in_1[3], ~in_1[4], ~in_1[5], ~in_1[6], in_1[7], ~in_1[8], ~in_1[9]);  // AND_Gate
  and and_2 (and_2_out, ~in_1[0], ~in_1[1], ~in_1[2], ~in_1[3], ~in_1[4], ~in_1[5], in_1[6], ~in_1[7], ~in_1[8], ~in_1[9]);  // AND_Gate
  and and_3 (and_3_out, ~in_1[0], ~in_1[1], ~in_1[2], in_1[3], ~in_1[4], ~in_1[5], ~in_1[6], ~in_1[7], ~in_1[8], ~in_1[9]);  // AND_Gate
  and and_4 (and_4_out, ~in_1[0], ~in_1[1], in_1[2], ~in_1[3], ~in_1[4], ~in_1[5], ~in_1[6], ~in_1[7], ~in_1[8], ~in_1[9]);  // AND_Gate
  or or_1 (out_2, and_1_out, and_2_out, and_3_out, and_4_out);
endmodule

module \Бит_0  (
  input  [9:0] in_1,
  output out_2
);

  wire and_1_out, and_2_out, and_3_out, and_4_out, and_5_out;

  and and_1 (and_1_out, ~in_1[0], ~in_1[1], ~in_1[2], ~in_1[3], ~in_1[4], ~in_1[5], ~in_1[6], ~in_1[7], ~in_1[8], in_1[9]);  // AND_Gate
  and and_2 (and_2_out, ~in_1[0], ~in_1[1], ~in_1[2], ~in_1[3], ~in_1[4], ~in_1[5], ~in_1[6], in_1[7], ~in_1[8], ~in_1[9]);  // AND_Gate
  and and_3 (and_3_out, ~in_1[0], ~in_1[1], ~in_1[2], ~in_1[3], ~in_1[4], in_1[5], ~in_1[6], ~in_1[7], ~in_1[8], ~in_1[9]);  // AND_Gate
  and and_4 (and_4_out, ~in_1[0], ~in_1[1], ~in_1[2], in_1[3], ~in_1[4], ~in_1[5], ~in_1[6], ~in_1[7], ~in_1[8], ~in_1[9]);  // AND_Gate
  and and_5 (and_5_out, ~in_1[0], in_1[1], ~in_1[2], ~in_1[3], ~in_1[4], ~in_1[5], ~in_1[6], ~in_1[7], ~in_1[8], ~in_1[9]);  // AND_Gate
  or or_1 (out_2, and_1_out, and_2_out, and_3_out, and_4_out, and_5_out);
endmodule

module \_10____7_сег  (
  input  [3:0] in_1,
  output [7:0] out_2
);

  wire and_1_out, and_2_out, and_3_out, and_4_out, and_5_out, and_6_out, and_7_out, and_8_out, and_9_out,
       and_10_out, and_11_out, not_1_out, not_2_out, not_3_out, not_4_out, not_5_out, not_6_out, not_7_out,
       not_8_out, not_9_out, not_10_out, not_11_out, not_12_out, not_13_out, not_14_out, not_15_out,
       not_16_out;

  not not_1 (not_1_out, in_1[1]);
  not not_2 (not_2_out, in_1[3]);
  not not_3 (not_3_out, in_1[3]);
  not not_4 (not_4_out, in_1[2]);
  not not_5 (not_5_out, in_1[2]);
  not not_6 (not_6_out, in_1[1]);
  not not_7 (not_7_out, in_1[2]);
  not not_8 (not_8_out, in_1[3]);
  not not_9 (not_9_out, in_1[2]);
  not not_10 (not_10_out, in_1[3]);
  not not_11 (not_11_out, in_1[1]);
  not not_12 (not_12_out, in_1[2]);
  not not_13 (not_13_out, in_1[3]);
  not not_14 (not_14_out, in_1[3]);
  not not_15 (not_15_out, in_1[1]);
  and and_1 (and_1_out, in_1[2], in_1[3]);
  and and_2 (and_2_out, not_1_out, not_2_out);
  and and_3 (and_3_out, in_1[2], not_3_out);
  not not_16 (not_16_out, in_1[3]);
  and and_4 (and_4_out, in_1[1], not_4_out);
  or or_1 (out_2[2], not_5_out, in_1[3], in_1[1]);
  and and_5 (and_5_out, not_6_out, in_1[2]);
  and and_6 (and_6_out, in_1[1], not_7_out);
  and and_7 (and_7_out, in_1[1], not_8_out);
  and and_8 (and_8_out, not_9_out, not_10_out);
  and and_9 (and_9_out, not_11_out, in_1[2], in_1[3]);
  and and_10 (and_10_out, in_1[1], not_12_out);
  and and_11 (and_11_out, in_1[1], not_13_out);
  or or_2 (out_2[6], not_14_out, in_1[1], in_1[0]);
  or or_3 (out_2[7], not_15_out, and_1_out);
  or or_4 (out_2[0], and_2_out, and_3_out);
  or or_5 (out_2[1], not_16_out, and_4_out, in_1[0]);
  or or_6 (out_2[4], and_5_out, and_6_out, and_7_out, in_1[0]);
  or or_7 (out_2[5], and_8_out, and_9_out, and_10_out, and_11_out, in_1[0]);

  assign out_2[3] = 1'b0;
endmodule

module _10____7 (
  input  [3:0] in_1,
  output [7:0] out_2
);

  wire demultiplexer_1_out0, demultiplexer_1_out1, demultiplexer_1_out2, demultiplexer_1_out3,
       demultiplexer_1_out4, demultiplexer_1_out5, demultiplexer_1_out6, demultiplexer_1_out7,
       demultiplexer_1_out8, demultiplexer_1_out9;
  wire [3:0] \перевод_в_10_ричную_1_out_11 ;

  Demultiplexer #(.select(4), .enable("false")) demultiplexer_1 (
    .out0(demultiplexer_1_out0), .out1(demultiplexer_1_out1), .out2(demultiplexer_1_out2),
    .out3(demultiplexer_1_out3), .out4(demultiplexer_1_out4), .out5(demultiplexer_1_out5),
    .out6(demultiplexer_1_out6), .out7(demultiplexer_1_out7), .out8(demultiplexer_1_out8),
    .out9(demultiplexer_1_out9), .in(1'b1), .sel(in_1));  // open: out10, out11, out12, out13, out14, out15
  // Probe on \перевод_в_10_ричную_1_out_11 
  // Probe on \перевод_в_10_ричную_1_out_11 
  \Перевод_в_10_ричную  \u_перевод_в_10_ричную_1  (
    ._0(demultiplexer_1_out0), ._1(demultiplexer_1_out1), ._2(demultiplexer_1_out2),
    ._3(demultiplexer_1_out3), ._4(demultiplexer_1_out4), ._5(demultiplexer_1_out5),
    ._6(demultiplexer_1_out6), ._7(demultiplexer_1_out7), ._8(demultiplexer_1_out8),
    ._9(demultiplexer_1_out9), .out_11(\перевод_в_10_ричную_1_out_11 ));
  \_10____7_сег  \u_10_7_сег_1  (.out_2(out_2), .in_1(\перевод_в_10_ричную_1_out_11 ));
endmodule
